# Fritzing sketch SmartGreen - scematics (saved by Fritzing 0.9.2b)
breadboards: 1

parts:
  Part1 = Arduino Pro Mini v13
  DHT1 = DHT22 Humidity and Temperature Sensor
  U1 = V_REG_LD1117VXX [package=78xxl]
  R1 = Resistor [tolerance=±5% resistance=10k package="1206 [SMD]"]
  U2 = ESP8266 WiFi Module [part_number=ESP8266]
  Power_plug1 = Power plug

nets:
  GND: Part1.GND, DHT1.GND, U1.GND, U2.GND, Power_plug1.GND
  VCC: Part1.VCC, U1.OUT, U2.VCC
  N1: Part1.D9_PWM, DHT1.DATA, R1.Pin_1
  N2: Part1.D8, U2.TXD
  N3: Part1.D7, U2.RXD
  N4: Part1.D6_PWM, U2.CH_PD
  N5: Part1.D5_PWM, DHT1.VDD, R1.Pin_0
  N6: U1.IN, Power_plug1.VCC

notes:
  5V DC Power source

custom parts:
  ESP8266 WiFi Module: Generic WiFi Module based on the ESP8266 with onboard PCB antenna and UART communications
